# Fritzing sketch Sketch (saved by Fritzing 0.9.10b)
circuit board: 8.46667cm x 5.64444cm
breadboards: 1

parts:
  Mod1 = Raspberry Pi Pico W
  S1 = Pushbutton [package="[THT]"]
  S2 = Pushbutton [package="[THT]"]
  S3 = Pushbutton [package="[THT]"]
  S4 = Pushbutton [package="[THT]"]
  LED1 = LED - 5mm [color="Red (633nm)" current=0.030 package="5 mm [THT]"]  # not connected
  LED2 = LED - 5mm [color="Yellow (595nm)" current=0.030 package="5 mm [THT]"]  # not connected
  LED3 = LED - 5mm [color="Green (555nm)" current=0.030 package="5 mm [THT]"]  # not connected
  LED4 = LED - 5mm [color="Blue (430nm)" current=0.030 package="5 mm [THT]"]  # not connected
  R1 = Resistor [tolerance=±5% power=0.25 resistance=200 package=THT]
  R2 = Resistor [tolerance=±5% power=0.25 resistance=200 package=THT]
  R3 = Resistor [tolerance=±5% power=0.25 resistance=200 package=THT]
  R4 = Resistor [tolerance=±5% power=0.25 resistance=200 package=THT]

nets:
  N1: Mod1.pin_3, Mod1.pin_8, Mod1.pin_13, Mod1.pin_18, Mod1.pin_23, Mod1.pin_28, Mod1.pin_33, Mod1.pin_38, S1.Pin_3, S1.Pin_4, S2.Pin_3, S2.Pin_4, S3.Pin_3, S3.Pin_4, S4.Pin_1, S4.Pin_2, S4.Pin_3, S4.Pin_4
  N2: Mod1.pin_4, R1.Pin_1
  N3: Mod1.pin_5, R2.Pin_1
  N4: Mod1.pin_6, R3.Pin_1
  N5: Mod1.pin_7, R4.Pin_1
  N6: Mod1.pin_9, S3.Pin_1, S3.Pin_2
  N7: Mod1.pin_10, S2.Pin_1, S2.Pin_2
  N8: Mod1.pin_11, S1.Pin_1, S1.Pin_2

custom parts:
  Raspberry Pi Pico W: Raspberry Pi Pico W. Based around the RP2040 microcontroller the Pico W is a low cost microcontroller device bringing Raspberry Pi quality, cost, and easy of use to the microcontroller space. The areas marked KEEPOUT in pcb silkscreen should not have traces running through them to avoid shorts on a soldered in module!
